# Fritzing sketch PN532-Wemos (saved by Fritzing 0.9.3b)

parts:
  WeMos_D1_Mini1 = WeMos D1 Mini
  Part1 = PN532 Elechouse RFID NFC Module V3

nets:
  5V: WeMos_D1_Mini1.5V, Part1.VCC
  N1: WeMos_D1_Mini1.D1, Part1.SCL
  N2: WeMos_D1_Mini1.D2, Part1.SDA
  N3: WeMos_D1_Mini1.G, Part1.GND

custom parts:
  PN532 Elechouse RFID NFC Module V3: NFC is a popular technology in recent years. We often heard this work while smart phone company such as Samsung or HTC introduces their latest high-end phones. Almost all the high-end phone in the market support NFC. Near field communication (NFC) is a set of standards for smart phones and similar devices to establish radio communication with each other by touching them together or bringing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
